# Fritzing sketch Motor Control fritzing (saved by Fritzing 0.9.3b)
breadboards: 1

parts:
  Part1 = Arduino Uno (Rev3)
  VCC1 = Battery
  Q1 = NPN-Transistor [package="TO92 [THT]"]
  D1 = Zener Diode [part_number=1N4732A breakdown_voltage=3.6V package="300 mil [THT]"]  # not connected
  R1 = Resistor [tolerance=±5% resistance=220 package="1206 [SMD]"]
  U1 = POT [package=3362u]
  M1 = DC Motor

nets:
  N1: Part1.A0, U1.S
  N2: Part1.D3_PWM, R1.Pin_0
  N3: Part1.GND, VCC1.-, Q1.E, U1.E
  N4: Part1.VIN, U1.A
  N5: VCC1.+, M1.pin_2
  N6: Q1.C, R1.Pin_1
