# Fritzing sketch Potentiometers fritzing (saved by Fritzing 0.9.3b)
breadboards: 1

parts:
  Part1 = Arduino Uno (Rev3)
  LCD1 = LCD screen  # not connected
  U1 = POT [package=pot_mammoth]
  LED1 = LED - 5mm [color="Red (633nm)" package="5 mm [THT]"]
  R1 = Resistor [tolerance=±5% resistance=220 package="1206 [SMD]"]

nets:
  N1: Part1.A3, U1.A
  N2: Part1.D5_PWM, LED1.cathode
  N3: Part1.5V, U1.E
  N4: Part1.GND, U1.S, R1.Pin_1
  N5: LED1.anode, R1.Pin_0

notes:
  SDA
  SCL
